// Digital circuit Alu.dig as structural Verilog
module Alu (
  input  [15:0] A,
  input  [15:0] B,
  input  [3:0] Sel,
  output [15:0] Out
);

  wire [15:0] add_1_s, and_1_out, barrelshifter_1_out, or_1_out, sub_1_s, xnor_1_out, xor_1_out;

  assign and_1_out = A & B;  // And and_1, 16 bits wide
  assign or_1_out = A | B;  // Or or_1, 16 bits wide
  assign xor_1_out = A ^ B;  // XOr xor_1, 16 bits wide
  assign xnor_1_out = ~(A ^ B);  // XNOr xnor_1, 16 bits wide
  Add #(.Bits(16)) add_1 (.a(A), .b(B), .c_i(1'b0), .s(add_1_s));  // open: c_o
  Sub #(.Bits(16)) sub_1 (.a(A), .b(B), .c_i(1'b0), .s(sub_1_s));  // open: c_o
  BarrelShifter #(.Bits(16), .barrelSigned("true")) barrelshifter_1 (.in(A), .shift(B[5:0]), .out(barrelshifter_1_out));
  Multiplexer #(.Selector_Bits(4), .Bits(16)) multiplexer_1 (
    .sel(Sel), .in_0(add_1_s), .in_1(sub_1_s), .in_2({16{1'b0}}), .in_3({16{1'b0}}), .in_4(and_1_out),
    .in_5(or_1_out), .in_6(xor_1_out), .in_7(xnor_1_out), .in_8(barrelshifter_1_out), .in_9({16{1'b0}}),
    .in_10({16{1'b0}}), .in_11({16{1'b0}}), .in_12({16{1'b0}}), .in_13({16{1'b0}}), .in_14({16{1'b0}}),
    .in_15({16{1'b0}}), .out(Out));
endmodule
