// Digital circuit AluStage.dig as structural Verilog
module AluStage (
  input  [15:0] A,
  input  [15:0] B,
  input  [15:0] Aux,
  input  [3:0] ALU_Sel,
  input  [7:0] Op,
  input  [2:0] C_Num,
  output [15:0] Data,
  output [2:0] Data_Num,
  output Data_NReady,
  output [15:0] Addr,
  output [7:0] Op_Next
);

  wire AD_SWAP, opsplit_1_jalr, opsplit_1_lui, opsplit_1_sw;
  wire [15:0] alu_1_out;

  Alu alu_1 (.A(A), .B(B), .Sel(ALU_Sel), .Out(alu_1_out));
  OpSplit opsplit_1 (
    .OP(Op), .LUI(opsplit_1_lui), .LW(Data_NReady), .SW(opsplit_1_sw), .JALR(opsplit_1_jalr));  // open: ALU, BEQ, BLT, ADDI
  Multiplexer #(.Bits(16)) multiplexer_1 (.sel(AD_SWAP), .in_0(alu_1_out), .in_1(Aux), .out(Data));
  Multiplexer #(.Bits(16)) multiplexer_2 (.sel(AD_SWAP), .in_0(Aux), .in_1(alu_1_out), .out(Addr));
  or or_1 (AD_SWAP, opsplit_1_lui, Data_NReady, opsplit_1_sw, opsplit_1_jalr);

  assign Data_Num = C_Num;
  assign Op_Next = Op;
endmodule
