// Digital circuit CountOnes.dig as structural Verilog
module CountOnes (
  input  [15:0] IN,
  output [4:0] OUT
);

  wire [1:0] I2_0, I2_1, I2_2, I2_3;
  wire [2:0] add_7_s, I3_0, I3_1;
  wire [3:3] add_7_c_o;

  Add add_1 (.a(IN[0]), .b(IN[1]), .c_i(IN[2]), .s(I2_0[0]), .c_o(I2_0[1]));
  Add add_2 (.a(IN[3]), .b(IN[4]), .c_i(IN[5]), .s(I2_1[0]), .c_o(I2_1[1]));
  Add add_3 (.a(IN[6]), .b(IN[7]), .c_i(IN[8]), .s(I2_2[0]), .c_o(I2_2[1]));
  Add add_4 (.a(IN[9]), .b(IN[10]), .c_i(IN[11]), .s(I2_3[0]), .c_o(I2_3[1]));
  Add #(.Bits(2)) add_5 (.a(I2_0), .b(I2_1), .c_i(IN[12]), .s(I3_0[1:0]), .c_o(I3_0[2]));
  Add #(.Bits(2)) add_6 (.a(I2_2), .b(I2_3), .c_i(IN[13]), .s(I3_1[1:0]), .c_o(I3_1[2]));
  Add #(.Bits(3)) add_7 (.a(I3_0), .b(I3_1), .c_i(IN[14]), .s(add_7_s), .c_o(add_7_c_o[3]));
  Add #(.Bits(4)) add_8 (.a({add_7_c_o[3], add_7_s}), .b(4'b0000), .c_i(IN[15]), .s(OUT[3:0]), .c_o(OUT[4]));

  // Other names for the same wires on the sheet: I1_0 = IN[0]; I1_1 = IN[1]; I1_2 = IN[2]; I1_3 = IN[3]; I1_4 = IN[4];
  //   I1_5 = IN[5]; I1_6 = IN[6]; I1_7 = IN[7]; I1_8 = IN[8]; I1_9 = IN[9]; I1_10 = IN[10]; I1_11 = IN[11];
  //   I1_12 = IN[12]; I1_13 = IN[13]; I1_14 = IN[14]; I1_15 = IN[15]
endmodule
