// Digital circuit Cpu16x.dig as structural Verilog
module Cpu16x (
  input  Clock,
  input  [15:0] Fetch_Data,
  input  Fetch_Ready,
  input  [15:0] Data_Data,
  input  Data_Ready,
  input  Reset,
  output [15:0] Fetch_Addr,
  output Fetch_Read,
  output Fetch_Write,
  output [15:0] Data_Addr,
  output Data_Read,
  output Data_Write
);

  wire alustage_1_data_nready, memstage_1_branch, undriven, undriven_2, undriven_3, undriven_4;
  wire [2:0] alustage_1_data_num, C_Num_out, Data_Num_out, decodestage_1_c_num, memstage_1_result_num;
  wire [3:0] ALU_Op_out, decodestage_1_alu_op;
  wire [7:0] alustage_1_op_next, decodestage_1_op_next, Op2_out, Op_out;
  wire [15:0] A_2_out, Addr_out, alustage_1_addr, alustage_1_data, Aux_out, B_2_out, Data_out,
       decodestage_1_a, decodestage_1_aux, decodestage_1_b, fetchstage_1_instr, fetchstage_1_instr_pc,
       Instr_out, memstage_1_result, PC_out;

  // Probe Branch_Addr on Addr_out
  // Probe Branch on memstage_1_branch
  FetchStage fetchstage_1 (
    .Addr(Addr_out), .Reset(Reset), .Branch(memstage_1_branch), .Clock(Clock), .NReady(undriven),
    .Bus_Addr(Fetch_Addr), .Bus_Data(Fetch_Data), .Bus_Read(Fetch_Read), .Bus_Write(Fetch_Write),
    .Bus_Ready(Fetch_Ready), .Instr(fetchstage_1_instr), .Instr_PC(fetchstage_1_instr_pc));
  PipelineReg #(.generic("Bits := 16;")) Instr (
    .Out(Instr_out), .Stall(undriven_2), .Branch(memstage_1_branch), .In(fetchstage_1_instr), .Clock(Clock),
    .NReady(undriven));
  PipelineReg #(.generic("Bits := 16;")) PC (
    .Out(PC_out), .Stall(undriven_2), .Branch(memstage_1_branch), .In(fetchstage_1_instr_pc), .Clock(Clock),
    .NReady(undriven));
  DecodeStage decodestage_1 (
    .Clock(Clock), .Instr(Instr_out), .PC(PC_out), .Result(memstage_1_result),
    .Result_Num(memstage_1_result_num), .Data(alustage_1_data), .Data_Num(alustage_1_data_num),
    .Data_NReady(alustage_1_data_nready), .NReady(undriven_2), .A(decodestage_1_a), .B(decodestage_1_b),
    .Aux(decodestage_1_aux), .C_NUM(decodestage_1_c_num), .ALU_OP(decodestage_1_alu_op),
    .Op_Next(decodestage_1_op_next));
  // Probe A on decodestage_1_a
  // Probe B on decodestage_1_b
  PipelineReg #(.generic("Bits := 16;")) A_2 (
    .Out(A_2_out), .Stall(undriven_3), .Branch(memstage_1_branch), .In(decodestage_1_a), .Clock(Clock),
    .NReady(undriven_2));
  PipelineReg #(.generic("Bits := 16;")) B_2 (
    .Out(B_2_out), .Stall(undriven_3), .Branch(memstage_1_branch), .In(decodestage_1_b), .Clock(Clock),
    .NReady(undriven_2));
  PipelineReg #(.generic("Bits := 16;")) Aux (
    .Out(Aux_out), .Stall(undriven_3), .Branch(memstage_1_branch), .In(decodestage_1_aux), .Clock(Clock),
    .NReady(undriven_2));
  PipelineReg #(.generic("Bits := 3;")) C_Num (
    .Out(C_Num_out), .Stall(undriven_3), .Branch(memstage_1_branch), .In(decodestage_1_c_num), .Clock(Clock),
    .NReady(undriven_2));
  PipelineReg #(.generic("Bits := 4;")) ALU_Op (
    .Out(ALU_Op_out), .Stall(undriven_3), .Branch(memstage_1_branch), .In(decodestage_1_alu_op),
    .Clock(Clock), .NReady(undriven_2));
  PipelineReg #(.generic("Bits := 8;")) Op (
    .Out(Op_out), .Stall(undriven_3), .Branch(memstage_1_branch), .In(decodestage_1_op_next), .Clock(Clock),
    .NReady(undriven_2));
  AluStage alustage_1 (
    .A(A_2_out), .B(B_2_out), .Aux(Aux_out), .ALU_Sel(ALU_Op_out), .Op(Op_out), .C_Num(C_Num_out),
    .Data(alustage_1_data), .Data_Num(alustage_1_data_num), .Data_NReady(alustage_1_data_nready),
    .Addr(alustage_1_addr), .Op_Next(alustage_1_op_next));
  PipelineReg #(.generic("Bits := 16;")) Data (
    .Out(Data_out), .Stall(undriven_4), .Branch(memstage_1_branch), .In(alustage_1_data), .Clock(Clock),
    .NReady(undriven_3));
  PipelineReg #(.generic("Bits := 3;")) Data_Num (
    .Out(Data_Num_out), .Stall(undriven_4), .Branch(memstage_1_branch), .In(alustage_1_data_num),
    .Clock(Clock), .NReady(undriven_3));
  PipelineReg #(.generic("Bits := 16;")) Addr (
    .Out(Addr_out), .Stall(undriven_4), .Branch(memstage_1_branch), .In(alustage_1_addr), .Clock(Clock),
    .NReady(undriven_3));
  PipelineReg #(.generic("Bits := 8;")) Op2 (
    .Out(Op2_out), .Stall(undriven_4), .Branch(memstage_1_branch), .In(alustage_1_op_next), .Clock(Clock),
    .NReady(undriven_3));
  MemStage memstage_1 (
    .Addr(Addr_out), .Data(Data_out), .Data_Num(Data_Num_out), .Op(Op2_out), .BUS_Addr(Data_Addr),
    .Bus_Data(Data_Data), .Bus_Read(Data_Read), .Bus_Write(Data_Write), .Bus_Ready(Data_Ready),
    .Result(memstage_1_result), .Result_Num(memstage_1_result_num), .Branch(memstage_1_branch),
    .NReady(undriven_4));
  // Probe Result on memstage_1_result
  // Probe Result_Num on memstage_1_result_num
endmodule
