// Digital circuit DecodeStage.dig as structural Verilog
module DecodeStage (
  input  Clock,
  input  [15:0] Instr,
  input  [15:0] PC,
  input  [15:0] Result,
  input  [2:0] Result_Num,
  input  [15:0] Data,
  input  [2:0] Data_Num,
  input  Data_NReady,
  input  NReady,
  output [15:0] A,
  output [15:0] B,
  output [15:0] Aux,
  output [2:0] C_NUM,
  output [3:0] ALU_OP,
  output [7:0] Op_Next
);

  wire A_Dst, A_EN, A_NStall, ALU_INSTR, ALU_SUB, and_1_out, and_2_out, AUX_IMM10, AUX_PC, AUX_PC_DIRECT,
       forwardingmux_3_active, forwardingmux_4_active, opsplit_1_addi, opsplit_1_beq, opsplit_1_blt,
       opsplit_1_lw, or_6_out;
  wire [3:0] multiplexer_2_out;
  wire [15:0] add_1_s, forwardingmux_1_out, forwardingmux_2_out, forwardingmux_3_out, IMM7,
       multiplexer_1_out, multiplexer_3_out, registerfile_1_a, registerfile_1_b;

  Decoder #(.Selector_Bits(3)) decoder_1 (
    .sel(Instr[15:13]), .out_0(Op_Next[0]), .out_1(Op_Next[1]), .out_2(Op_Next[2]), .out_3(Op_Next[3]),
    .out_4(Op_Next[4]), .out_5(Op_Next[5]), .out_6(Op_Next[6]), .out_7(Op_Next[7]));
  BitExtender #(.inputBits(7)) bitextender_1 (.in(Instr[6:0]), .out(IMM7));
  RegisterFile registerfile_1 (
    .Result(Result), .Result_Num(Result_Num), .A_Num(Instr[12:10]), .B_Num(Instr[9:7]), .Clock(Clock),
    .A(registerfile_1_a), .B(registerfile_1_b));
  OpSplit opsplit_1 (
    .OP(Op_Next), .ALU(ALU_INSTR), .LUI(AUX_IMM10), .BEQ(opsplit_1_beq), .BLT(opsplit_1_blt),
    .LW(opsplit_1_lw), .ADDI(opsplit_1_addi), .JALR(AUX_PC_DIRECT));  // open: SW
  or or_1 (A_EN, ALU_INSTR, opsplit_1_beq, opsplit_1_blt);
  ForwardingMux forwardingmux_1 (
    .A(registerfile_1_a), .F(Result), .A_Num(Instr[12:10]), .F_Num(Result_Num), .Out(forwardingmux_1_out));  // open: Active
  ForwardingMux forwardingmux_2 (
    .A(registerfile_1_b), .F(Result), .A_Num(Instr[9:7]), .F_Num(Result_Num), .Out(forwardingmux_2_out));  // open: Active
  or or_2 (AUX_PC, opsplit_1_beq, opsplit_1_blt, AUX_PC_DIRECT);
  ForwardingMux forwardingmux_3 (
    .A(forwardingmux_1_out), .F(Data), .A_Num(Instr[12:10]), .F_Num(Data_Num), .Out(forwardingmux_3_out),
    .Active(forwardingmux_3_active));
  ForwardingMux forwardingmux_4 (
    .A(forwardingmux_2_out), .F(Data), .A_Num(Instr[9:7]), .F_Num(Data_Num), .Out(B),
    .Active(forwardingmux_4_active));
  or or_3 (A_Dst, AUX_IMM10, opsplit_1_lw, opsplit_1_addi, AUX_PC_DIRECT);
  or or_4 (ALU_SUB, opsplit_1_beq, opsplit_1_blt);
  or or_5 (A_NStall, AUX_IMM10, opsplit_1_lw, opsplit_1_addi, AUX_PC_DIRECT);
  and and_1 (and_1_out, forwardingmux_3_active, Data_NReady, ~A_NStall);  // And
  and and_2 (and_2_out, forwardingmux_4_active, Data_NReady, ~AUX_IMM10);  // And
  Multiplexer #(.Bits(16)) multiplexer_1 (
    .sel(AUX_IMM10), .in_0(forwardingmux_3_out), .in_1({Instr[9:0], {6{1'b0}}}), .out(multiplexer_1_out));
  Add #(.Bits(16)) add_1 (.a(PC), .b(IMM7), .c_i(1'b0), .s(add_1_s));  // open: c_o
  or or_6 (or_6_out, and_2_out, and_1_out);
  Multiplexer #(.Bits(4)) multiplexer_2 (.sel(ALU_SUB), .in_0(4'b0000), .in_1(4'b0001), .out(multiplexer_2_out));
  DiodeForward diodeforward_1 (.in(or_6_out), .out(NReady));
  Multiplexer #(.Bits(16)) multiplexer_3 (.sel(AUX_PC_DIRECT), .in_0(add_1_s), .in_1(PC), .out(multiplexer_3_out));
  Multiplexer #(.Bits(16)) multiplexer_4 (.sel(A_EN), .in_0(IMM7), .in_1(forwardingmux_3_out), .out(A));
  Multiplexer #(.Bits(16)) multiplexer_5 (.sel(AUX_PC), .in_0(multiplexer_1_out), .in_1(multiplexer_3_out), .out(Aux));
  Multiplexer #(.Selector_Bits(2), .Bits(3)) multiplexer_6 (
    .sel({ALU_INSTR, A_Dst}), .in_0(3'b000), .in_1(Instr[12:10]), .in_2(Instr[6:4]), .in_3(3'b000));  // open: out
  Multiplexer #(.Bits(4)) multiplexer_7 (.sel(ALU_INSTR), .in_0(multiplexer_2_out), .in_1(Instr[3:0]), .out(ALU_OP));

  // Other names for the same wires on the sheet: B_NStall = AUX_IMM10; C_DST = ALU_INSTR; ALU_NUM[3:0] = Instr[3:0];
  //   IMM10[15:6] = Instr[9:0]; C_NUM_t[2:0] = Instr[6:4]; A_NUM[2:0] = Instr[12:10]; OP_NUM[2:0] = Instr[15:13]
endmodule
