// Digital circuit Divider.dig as structural Verilog
module Divider (
  input  [15:0] A,
  input  [15:0] B,
  input  CLK,
  input  GO,
  output [15:0] R,
  output [15:0] Q,
  output NREADY
);

  wire comparator_1_eq, EN, START, sub_1_c_o, sub_2_c_o;
  wire [0:0] multiplexer_1_out_2;
  wire [3:0] CTR_q, sub_1_s;
  wire [14:0] multiplexer_2_out;
  wire [15:0] A_q, R_q, register_1_q, sub_2_s;
  wire [15:1] multiplexer_1_out;
  wire [15:15] multiplexer_2_out_2, multiplexer_4_out;

  Register #(.Bits(16)) u_A (.D({multiplexer_1_out, 1'b0}), .C(CLK), .en(EN), .Q(A_q));
  Multiplexer #(.Bits(16)) multiplexer_1 (
    .sel(START), .in_0(A_q), .in_1(A), .out({multiplexer_1_out_2[0], multiplexer_1_out}));
  Register #(.Bits(16)) u_R (.D(R), .C(CLK), .en(EN), .Q(R_q));
  Register #(.Bits(4)) CTR (.D(sub_1_s), .C(CLK), .en(EN), .Q(CTR_q));
  Sub #(.Bits(4)) sub_1 (.a(CTR_q), .b(4'b0001), .c_i(1'b0), .s(sub_1_s), .c_o(sub_1_c_o));
  Multiplexer #(.Bits(16)) multiplexer_2 (
    .sel(START), .in_0(R_q), .in_1({16{1'b0}}), .out({multiplexer_2_out_2[15], multiplexer_2_out}));
  Comparator #(.Bits(4)) comparator_1 (.a(sub_1_s), .b(4'b0000), .eq(comparator_1_eq));  // open: gt, lt
  or or_1 (EN, ~sub_1_c_o, GO);  // Or
  and and_1 (START, sub_1_c_o, GO);
  Sub #(.Bits(16)) sub_2 (
    .a({multiplexer_2_out, multiplexer_1_out_2[0]}), .b(B), .c_i(1'b0), .s(sub_2_s), .c_o(sub_2_c_o));
  and and_2 (NREADY, ~comparator_1_eq, GO);  // And
  not not_1 (Q[0], sub_2_c_o);
  Multiplexer #(.Bits(16)) multiplexer_3 (
    .sel(Q[0]), .in_0({multiplexer_2_out, multiplexer_1_out_2[0]}), .in_1(sub_2_s), .out(R));
  Register #(.Bits(16)) register_1 (.D(Q), .C(CLK), .en(EN), .Q(register_1_q));
  Multiplexer #(.Bits(16)) multiplexer_4 (
    .sel(START), .in_0(register_1_q), .in_1({16{1'b0}}), .out({multiplexer_4_out[15], Q[15:1]}));
endmodule
