// Digital circuit FetchStage.dig as structural Verilog
module FetchStage (
  input  NReady,
  input  [15:0] Bus_Data,
  input  [15:0] Addr,
  input  Branch,
  input  Clock,
  input  Bus_Ready,
  input  Reset,
  output [15:0] Bus_Addr,
  output [15:0] Instr,
  output [15:0] Instr_PC,
  output Bus_Read,
  output Bus_Write
);

  wire not_1_out, or_1_out;
  wire [15:0] add_1_s, multiplexer_1_out, multiplexer_2_out;

  Add #(.Bits(16)) add_1 (.a(Bus_Addr), .b({16{1'b0}}), .c_i(1'b1), .s(add_1_s));  // open: c_o
  Multiplexer #(.Bits(16)) multiplexer_1 (.sel(Branch), .in_0(add_1_s), .in_1(Addr), .out(multiplexer_1_out));
  Multiplexer #(.Bits(16)) multiplexer_2 (
    .sel(Reset), .in_0(multiplexer_1_out), .in_1(16'h4000), .out(multiplexer_2_out));
  or or_1 (or_1_out, Reset, Branch, ~NReady);  // Or
  Register #(.Bits(16), .isProgramCounter("true")) PC (.D(multiplexer_2_out), .C(Clock), .en(or_1_out), .Q(Bus_Addr));
  PullDown pulldown_1 (.out(NReady));
  DiodeForward diodeforward_1 (.in(not_1_out), .out(NReady));
  not not_1 (not_1_out, Bus_Ready);
  PullDown pulldown_2 (.out(Bus_Ready));

  assign Bus_Read = 1'b1;
  assign Bus_Write = 1'b0;
  assign Instr = Bus_Data;
  assign Instr_PC = Bus_Addr;
endmodule
