// Digital circuit ForwardingMux.dig as structural Verilog
module ForwardingMux (
  input  [15:0] A,
  input  [15:0] F,
  input  [2:0] A_Num,
  input  [2:0] F_Num,
  output [15:0] Out,
  output Active
);

  wire comparator_1_eq, comparator_2_eq;

  Comparator #(.Bits(3)) comparator_1 (.a(F_Num), .b(A_Num), .eq(comparator_1_eq));  // open: gt, lt
  Comparator #(.Bits(3)) comparator_2 (.a(F_Num), .b(3'b000), .eq(comparator_2_eq));  // open: gt, lt
  and and_1 (Active, comparator_1_eq, ~comparator_2_eq);  // And
  Multiplexer #(.Bits(16)) multiplexer_1 (.sel(Active), .in_0(A), .in_1(F), .out(Out));
endmodule
