// Digital circuit MemStage.dig as structural Verilog
module MemStage (
  input  [15:0] Addr,
  input  [15:0] Data,
  input  [15:0] Bus_Data,
  input  [2:0] Data_Num,
  input  [7:0] Op,
  input  NReady,
  input  Bus_Ready,
  output [15:0] BUS_Addr,
  output [15:0] Result,
  output [2:0] Result_Num,
  output Bus_Read,
  output Bus_Write,
  output Branch
);

  wire and_1_out, and_2_out, and_3_out, comparator_1_eq, not_1_out, opsplit_1_beq, opsplit_1_blt,
       opsplit_1_jalr, or_2_out;

  OpSplit opsplit_1 (
    .OP(Op), .BEQ(opsplit_1_beq), .BLT(opsplit_1_blt), .LW(Bus_Read), .SW(Bus_Write), .JALR(opsplit_1_jalr));  // open: ALU, LUI, ADDI
  Comparator #(.Bits(16)) comparator_1 (.a(Data), .b({16{1'b0}}), .eq(comparator_1_eq));  // open: gt, lt
  and and_1 (and_1_out, comparator_1_eq, opsplit_1_beq);
  and and_2 (and_2_out, Data[15], opsplit_1_blt);
  or or_1 (Branch, and_1_out, opsplit_1_jalr, and_2_out);
  assign Bus_Data = not_1_out ? Data : 16'bz;  // Driver driver_1
  not not_1 (not_1_out, Bus_Read);
  or or_2 (or_2_out, Bus_Read, Bus_Write);
  and and_3 (and_3_out, ~Bus_Ready, or_2_out);  // And
  PullDown pulldown_1 (.out(Bus_Ready));
  DiodeForward diodeforward_1 (.in(and_3_out), .out(NReady));
  PullDown pulldown_2 (.out(NReady));

  assign BUS_Addr = Addr;
  assign Result = Bus_Data;
  assign Result_Num = Data_Num;
endmodule
