// Digital circuit Multiplier.dig as structural Verilog
module Multiplier (
  input  Go,
  input  [15:0] A,
  input  [15:0] B,
  input  CLK,
  output [15:0] OUT
);

  wire comparator_1_eq, EN, START;
  wire [0:0] B_q;
  wire [3:0] add_2_s, CTR_q;
  wire [14:0] multiplexer_3_out;
  wire [15:0] A_q, add_1_s, multiplexer_1_out, multiplexer_2_out, P_q;

  Multiplexer #(.Bits(16)) multiplexer_1 (
    .sel(START), .in_0({1'b0, multiplexer_3_out}), .in_1({16{1'b0}}), .out(multiplexer_1_out));
  Multiplexer #(.Bits(16)) multiplexer_2 (.sel(START), .in_0(OUT), .in_1(B), .out(multiplexer_2_out));
  Register #(.Bits(16)) P (.D(multiplexer_1_out), .C(CLK), .en(EN), .Q(P_q));
  Register #(.Bits(16)) u_A (.D(A), .C(CLK), .en(START), .Q(A_q));
  Register #(.Bits(16)) u_B (.D(multiplexer_2_out), .C(CLK), .en(EN), .Q({OUT[14:0], B_q[0]}));
  Register #(.Bits(4)) CTR (.D(add_2_s), .C(CLK), .en(EN), .Q(CTR_q));
  Add #(.Bits(16)) add_1 (.a(P_q), .b(A_q), .c_i(1'b0), .s(add_1_s));  // open: c_o
  Comparator #(.Bits(4)) comparator_1 (.a(CTR_q), .b(4'b0000), .eq(comparator_1_eq));  // open: gt, lt
  Multiplexer #(.Bits(16)) multiplexer_3 (.sel(B_q[0]), .in_0(P_q), .in_1(add_1_s), .out({multiplexer_3_out, OUT[15]}));
  Add #(.Bits(4)) add_2 (.a(CTR_q), .b(4'b0001), .c_i(1'b0), .s(add_2_s));  // open: c_o
  or or_1 (EN, ~comparator_1_eq, Go);  // Or
  and and_1 (START, comparator_1_eq, Go);
endmodule
