// Digital circuit OpSplit.dig as structural Verilog
module OpSplit (
  input  [7:0] OP,
  output ALU,
  output LUI,
  output BEQ,
  output BLT,
  output LW,
  output SW,
  output ADDI,
  output JALR
);


  assign ADDI = OP[6];
  assign ALU = OP[0];
  assign BEQ = OP[2];
  assign BLT = OP[3];
  assign JALR = OP[7];
  assign LUI = OP[1];
  assign LW = OP[4];
  assign SW = OP[5];
endmodule
