// Digital circuit PipelineReg.dig as structural Verilog
module PipelineReg (
  input  [15:0] In,
  input  Clock,
  input  Stall,
  input  NReady,
  input  Branch,
  output Out
);

  wire or_1_out;
  wire [15:0] multiplexer_1_out;
  wire [15:5] undriven;

  Multiplexer #(.Bits(16), .generic("this.Bits=args.Bits;")) multiplexer_1 (
    .sel(NReady), .in_0(In), .in_1({undriven, {5{1'b0}}}), .out(multiplexer_1_out));
  PullDown pulldown_1 (.out(NReady));
  or or_1 (or_1_out, ~Stall, Branch);  // Or
  DiodeForward diodeforward_1 (.in(Stall), .out(NReady));
  DiodeForward diodeforward_2 (.in(Branch), .out(NReady));
  Register #(.generic("this.Bits=args.Bits;")) register_1 (.D(multiplexer_1_out), .C(Clock), .en(or_1_out), .Q(Out));
  // Pins of 5 and 16 bits meet at {undriven, {5{1'b0}}}
endmodule

/* Code that sets the parameters or builds the circuit:
Bits := 5;
*/
