// Digital circuit RegisterFile.dig as structural Verilog
module RegisterFile (
  input  [15:0] Result,
  input  [2:0] Result_Num,
  input  Clock,
  input  [2:0] A_Num,
  input  [2:0] B_Num,
  output [15:0] A,
  output [15:0] B
);

  wire comparator_1_eq, not_1_out;

  Comparator #(.Bits(3)) comparator_1 (.a(3'b000), .b(Result_Num), .eq(comparator_1_eq));  // open: gt, lt
  not not_1 (not_1_out, comparator_1_eq);
  RegisterFile #(.AddrBits(3), .Bits(16)) registerfile_1 (
    .Din(Result), .we(not_1_out), .Rw(Result_Num), .C(Clock), .Ra(A_Num), .Rb(B_Num), .Da(A), .Db(B));
endmodule
