// Digital circuit Top.dig as structural Verilog
module Top (
  input  clk,
  input  Reset
);

  wire and_1_out, and_2_out, and_3_out, comparator_1_eq, comparator_2_eq, cpu16x_1_data_read,
       cpu16x_1_data_write, cpu16x_1_fetch_read, diodeforward_1_out, diodeforward_2_out;
  wire [5:0] cpu16x_1_data_addr_2;
  wire [9:0] cpu16x_1_data_addr;
  wire [15:0] cpu16x_1_fetch_addr, driver_1_out, driver_2_out, ramasync_1_q, rom_1_d;

  Cpu16x cpu16x_1 (
    .Clock(clk), .Reset(Reset), .Fetch_Addr(cpu16x_1_fetch_addr), .Fetch_Data(driver_1_out),
    .Fetch_Read(cpu16x_1_fetch_read), .Fetch_Ready(diodeforward_2_out),
    .Data_Addr({cpu16x_1_data_addr_2, cpu16x_1_data_addr}), .Data_Data(driver_2_out),
    .Data_Read(cpu16x_1_data_read), .Data_Write(cpu16x_1_data_write), .Data_Ready(diodeforward_1_out));  // open: Fetch_Write
  Comparator #(.Bits(6)) comparator_1 (.a(cpu16x_1_data_addr_2), .b({6{1'b0}}), .eq(comparator_1_eq));  // open: gt, lt
  DiodeForward diodeforward_1 (.in(comparator_1_eq), .out(diodeforward_1_out));
  Comparator #(.Bits(8)) comparator_2 (.a(cpu16x_1_fetch_addr[15:8]), .b(8'h40), .eq(comparator_2_eq));  // open: gt, lt
  DiodeForward diodeforward_2 (.in(comparator_2_eq), .out(diodeforward_2_out));
  ROM #(.AddrBits(8), .isProgramMemory("true"), .Bits(16)) rom_1 (
    .A(cpu16x_1_fetch_addr[7:0]), .sel(comparator_2_eq), .D(rom_1_d));
  and and_1 (and_1_out, comparator_2_eq, cpu16x_1_fetch_read);
  and and_2 (and_2_out, comparator_1_eq, cpu16x_1_data_write);
  RAMAsync #(.AddrBits(10), .Bits(16)) ramasync_1 (
    .A(cpu16x_1_data_addr), .D(driver_2_out), .we(and_2_out), .Q(ramasync_1_q));
  and and_3 (and_3_out, comparator_1_eq, cpu16x_1_data_read);
  assign driver_1_out = and_1_out ? rom_1_d : 16'bz;  // Driver driver_1
  assign driver_2_out = and_3_out ? ramasync_1_q : 16'bz;  // Driver driver_2

  // Notes on the sheet:
  //   contents of rom_1 (hex, n*v repeats v):
  //   2400,c480,2800,c920,cc10,9080,b100,c481,c901,cdff,61fa,407f
endmodule
