// Digital circuit countones4.dig as structural Verilog
module countones4 (
  input  A,
  input  B,
  input  C,
  input  D,
  output [2:0] Q
);

  wire [1:0] add_1_s;

  Add add_1 (.a(A), .b(B), .c_i(C), .s(add_1_s[0]), .c_o(add_1_s[1]));
  Add #(.Bits(2)) add_2 (.a(add_1_s), .b(2'b00), .c_i(D), .s(Q[1:0]), .c_o(Q[2]));
endmodule
